# Fritzing sketch Control Unit (saved by Fritzing 0.9.7b)
breadboards: 1

parts:
  Part1 = Arduino Micro (Rev3)
  OBS1 = Momentary Switch [package=ksa_sealed_tac_switch]
  OBS2 = Momentary Switch [package=ksa_sealed_tac_switch]
  OBS3 = Momentary Switch [package=ksa_sealed_tac_switch]
  OBS4 = Momentary Switch [package=ksa_sealed_tac_switch]
  OBS5 = Momentary Switch [package=ksa_sealed_tac_switch]
  OBS6 = Momentary Switch [package=ksa_sealed_tac_switch]
  OBS7 = Momentary Switch [package=ksa_sealed_tac_switch]
  OBS8 = Momentary Switch [package=ksa_sealed_tac_switch]
  Streaming? = Momentary Switch [package=ksa_sealed_tac_switch]
  Recording? = Momentary Switch [package=ksa_sealed_tac_switch]
  Muted? = Momentary Switch [package=ksa_sealed_tac_switch]
  Back_Slide = Momentary Switch [package=ksa_sealed_tac_switch]
  Forw_Slide = Momentary Switch [package=ksa_sealed_tac_switch]
  RE1 = KY-040 Rotary encoder [package=THT]
  R2 = Resistor [tolerance=±5% resistance=1k package="1206 [SMD]"]
  R3 = Resistor [tolerance=±5% resistance=1k package="1206 [SMD]"]
  R4 = Resistor [tolerance=±5% resistance=1k package="1206 [SMD]"]
  R5 = Resistor [tolerance=±5% resistance=1k package="1206 [SMD]"]
  R6 = Resistor [tolerance=±5% resistance=1k package="1206 [SMD]"]
  R7 = Resistor [tolerance=±5% resistance=1k package="1206 [SMD]"]
  R8 = Resistor [tolerance=±5% resistance=1k package="1206 [SMD]"]
  R9 = Resistor [tolerance=±5% resistance=1k package="1206 [SMD]"]
  R10 = Resistor [tolerance=±5% resistance=1k package="1206 [SMD]"]
  R11 = Resistor [tolerance=±5% resistance=1k package="1206 [SMD]"]
  R12 = Resistor [tolerance=±5% resistance=1k package="1206 [SMD]"]
  R13 = Resistor [tolerance=±5% resistance=1k package="1206 [SMD]"]
  R14 = Resistor [tolerance=±5% resistance=1k package="1206 [SMD]"]
  Cable = Header 8 [package=1x08_smd]

nets:
  N1: Part1.D0/RX, Cable.2
  N2: Part1.RESET, Cable.3
  GND: Part1.GND, OBS1.1, OBS2.1, OBS3.1, OBS4.1, OBS5.1, OBS6.1, OBS7.1, OBS8.1, Streaming?.1, Recording?.1, Muted?.1, Back_Slide.1, Forw_Slide.1, RE1.GND, Cable.8
  N3: Part1.D2/SDA, Muted?.3, R12.Pin_0
  N4: Part1.D3/SCL, Recording?.3, R13.Pin_0
  N5: Part1.D4_PWM/A6, Streaming?.3, R14.Pin_0
  N6: Part1.D5_PWM, OBS8.3, R9.Pin_0
  N7: Part1.D6_PWM/A7, OBS7.3, R8.Pin_0
  N8: Part1.D7, OBS6.3, R7.Pin_0
  N9: Part1.D8_PWM/A8, OBS5.3, R6.Pin_0
  N10: Part1.D9_PWM/A9, OBS4.3, R4.Pin_0
  N11: Part1.D10_PWM/A10, OBS3.3, R3.Pin_0
  N12: Part1.D11_PWM, OBS2.3, R5.Pin_0
  N13: Part1.D12_PWM/A11, OBS1.3, R2.Pin_0
  5V: Part1.5V, RE1.Vcc, R2.Pin_1, R3.Pin_1, R4.Pin_1, R5.Pin_1, R6.Pin_1, R7.Pin_1, R8.Pin_1, R9.Pin_1, R10.Pin_1, R11.Pin_1, R12.Pin_1, R13.Pin_1, R14.Pin_1, Cable.1
  N14: Part1.A5, Cable.6
  N15: Part1.A4, Cable.5
  N16: Part1.A3, Back_Slide.3, R11.Pin_0
  N17: Part1.A2, Forw_Slide.3, R10.Pin_0
  N18: Part1.A1, RE1.DT
  N19: Part1.A0, RE1.CLK
  N20: Part1.D13_PWM, Cable.4

custom parts:
  KY-040 Rotary encoder: KY-040 Rotary Encoder with switch on breakout borad from AZ Delivery
