# Fritzing sketch Display Unit (saved by Fritzing 0.9.7b)
breadboards: 2

parts:
  OBS2 = LED - 5mm [color="Red (633nm)" current=0.030 package="5 mm [THT]"]
  OBS3 = LED - 5mm [color="Red (633nm)" current=0.030 package="5 mm [THT]"]
  OBS6 = LED - 5mm [color="Red (633nm)" current=0.030 package="5 mm [THT]"]
  OBS5 = LED - 5mm [color="Red (633nm)" current=0.030 package="5 mm [THT]"]
  OBS4 = LED - 5mm [color="Red (633nm)" current=0.030 package="5 mm [THT]"]
  OBS8 = LED - 5mm [color="Red (633nm)" current=0.030 package="5 mm [THT]"]
  OBS7 = LED - 5mm [color="Red (633nm)" current=0.030 package="5 mm [THT]"]
  OBS1 = LED - 5mm [color="Red (633nm)" current=0.030 package="5 mm [THT]"]
  R1 = Resistor [tolerance=±5% resistance=1k package="2010 [SMD]"]
  R2 = Resistor [tolerance=±5% resistance=1k package="2010 [SMD]"]
  R3 = Resistor [tolerance=±5% resistance=1k package="2010 [SMD]"]
  R4 = Resistor [tolerance=±5% resistance=1k package="2010 [SMD]"]
  R5 = Resistor [tolerance=±5% resistance=1k package="2010 [SMD]"]
  R6 = Resistor [tolerance=±5% resistance=1k package="2010 [SMD]"]
  R7 = Resistor [tolerance=±5% resistance=1k package="2010 [SMD]"]
  R8 = Resistor [tolerance=±5% resistance=1k package="2010 [SMD]"]
  Muted? = LED - 5mm [color="Yellow (595nm)" current=0.030 package="5 mm [THT]"]
  Recording? = LED - 5mm [color="Yellow (595nm)" current=0.030 package="5 mm [THT]"]
  R9 = Resistor [tolerance=±5% resistance=1k package="2010 [SMD]"]
  R10 = Resistor [tolerance=±5% resistance=1k package="2010 [SMD]"]
  IC2 = 74LS138
  Cable = Header 8 [package=1x08_smd]

nets:
  N1: OBS2.cathode, IC2.connector13
  N2: OBS2.anode, R2.Pin_1
  N3: OBS3.cathode, IC2.connector12
  N4: OBS3.anode, R3.Pin_1
  N5: OBS6.cathode, IC2.connector9
  N6: OBS6.anode, R6.Pin_1
  N7: OBS5.cathode, IC2.connector10
  N8: OBS5.anode, R5.Pin_1
  N9: OBS4.cathode, IC2.connector11
  N10: OBS4.anode, R4.Pin_1
  N11: OBS8.cathode, IC2.connector6
  N12: OBS8.anode, R8.Pin_1
  N13: OBS7.cathode, IC2.connector8
  N14: OBS7.anode, R7.Pin_1
  N15: OBS1.cathode, IC2.connector14
  N16: OBS1.anode, R1.Pin_1
  N17: R1.Pin_0, R2.Pin_0, R3.Pin_0, R4.Pin_0, R5.Pin_0, R6.Pin_0, R7.Pin_0, R8.Pin_0, R9.Pin_0, R10.Pin_0, IC2.connector3, IC2.connector4, IC2.connector7, Cable.8
  N18: Muted?.cathode, Cable.6
  N19: Muted?.anode, R9.Pin_1
  N20: Recording?.cathode, Cable.5
  N21: Recording?.anode, R10.Pin_1
  N22: IC2.connector0, Cable.2
  N23: IC2.connector1, Cable.3
  N24: IC2.connector2, Cable.4
  N25: IC2.connector5, IC2.connector15, Cable.1
